# Fritzing sketch nanokeyer (saved by Fritzing 0.7.10b)
breadboards: 1

parts:
  U1 = Ardweeny
  S1 = Pushbutton [package="[THT]"]
  S2 = Pushbutton [package="[THT]"]
  S3 = Pushbutton [package="[THT]"]
  S4 = Pushbutton [package="[THT]"]
  TRS1 = Audio Jack (TRS) 3.5mm [package="PG203J [THT]"]
  Power_plug1 = Power plug
  SPKR1 = Loudspeaker
  R1 = 10k Ω Resistor [package=THT]
  C1 = Ceramic Capacitor [capacitance="100 nF" package="1206 [SMD, multilayer]"]

nets:
  N1: U1.Pin_6, TRS1.Tip
  N2: U1.Pin_7, Power_plug1.VCC
  GND: U1.Pin_8, U1.Pin_22, S1.Pin_1, S1.Pin_2, S2.Pin_1, S2.Pin_2, S3.Pin_1, S3.Pin_2, S4.Pin_1, S4.Pin_2, TRS1.Sleeve, Power_plug1.GND, SPKR1.pin1, C1.0
  N3: U1.Pin_11, TRS1.Ring
  N4: U1.Pin_12, R1.Pin_0
  N5: U1.Pin_14, S1.Pin_3, S1.Pin_4
  N6: U1.Pin_15, S2.Pin_3, S2.Pin_4
  N7: U1.Pin_16, S3.Pin_3, S3.Pin_4
  N8: U1.Pin_17, S4.Pin_3, S4.Pin_4
  N9: SPKR1.pin2, R1.Pin_1, C1.1

notes:
  Tone Up/Down
  QRS/QRQ
  Key: Dit=Tip, Dah=Ring
  R1: 10k
  C1: 0.01uF (103)

custom parts:
  Ardweeny: Solarbotics Ardweeny
